# Fritzing sketch PortfolioCircuitLayout (saved by Fritzing 0.9.2b)
breadboards: 1

parts:
  Part1 = Arduino Nano (Rev3.0)
  S1 = Pushbutton [package="[THT]"]
  S2 = Pushbutton [package="[THT]"]
  S3 = Pushbutton [package="[THT]"]
  S4 = Pushbutton [package="[THT]"]
  S5 = Pushbutton [package="[THT]"]
  S6 = Pushbutton [package="[THT]"]
  S7 = Pushbutton [package="[THT]"]
  S8 = Pushbutton [package="[THT]"]
  S9 = Pushbutton [package="[THT]"]
  S10 = Pushbutton [package="[THT]"]
  R1 = Resistor [tolerance=±5% resistance=330 package=THT]
  R2 = Resistor [tolerance=±5% resistance=330 package=THT]
  R3 = Resistor [tolerance=±5% resistance=330 package=THT]
  R4 = Resistor [tolerance=±5% resistance=330 package=THT]
  J1 = Basic Force Sensing Resistor (FSR) [package=THT]
  J2 = Basic Force Sensing Resistor (FSR) [package=THT]
  J3 = Basic Force Sensing Resistor (FSR) [package=THT]
  J4 = Basic Force Sensing Resistor (FSR) [package=THT]

nets:
  N1: Part1.GND, S1.Pin_1, S1.Pin_2, S2.Pin_1, S2.Pin_2, S3.Pin_2, S4.Pin_1, S4.Pin_2, S5.Pin_1, S5.Pin_2, S6.Pin_1, S6.Pin_2, S7.Pin_1, S7.Pin_2, S8.Pin_1, S8.Pin_2, S9.Pin_1, S9.Pin_2, S10.Pin_2, R1.Pin_0, R2.Pin_0, R3.Pin_0, R4.Pin_0
  N2: Part1.D2, S10.Pin_4
  N3: Part1.D3, S9.Pin_3, S9.Pin_4
  N4: Part1.D4, S8.Pin_3, S8.Pin_4
  N5: Part1.D5, S7.Pin_4
  N6: Part1.D6, S6.Pin_4
  N7: Part1.D7, S5.Pin_3, S5.Pin_4
  N8: Part1.D8, S4.Pin_4
  N9: Part1.D9, S3.Pin_4
  N10: Part1.D10, S2.Pin_3, S2.Pin_4
  N11: Part1.D11/MOSI, S1.Pin_3, S1.Pin_4
  N12: Part1.5V, J1.pin_1, J2.pin_1, J3.pin_1, J4.pin_1
  N13: Part1.A3, R2.Pin_1, J2.pin_0
  N14: Part1.A2, R3.Pin_1, J3.pin_0
  N15: Part1.A1, R1.Pin_1, J4.pin_0
  N16: Part1.A0, R4.Pin_1, J1.pin_0
